// Logisim project workshop.circ as structural Verilog: 3 circuits, main circuit main
module main (
  input  N,
  input  E,
  input  S,
  input  W,
  output out_5
);

  wire and_1_out, and_2_out, and_3_out, and_4_out, xor_1_out, xor_2_out;

  xor xor_1 (xor_1_out, N, E);
  and and_1 (and_1_out, N, E);
  xor xor_2 (xor_2_out, S, W);
  and and_2 (and_2_out, S, W);
  and and_3 (and_3_out, xor_1_out, and_2_out);
  and and_4 (and_4_out, and_1_out, xor_2_out);
  or or_1 (out_5, and_3_out, and_4_out);
endmodule

module other (
  input  N,
  input  E,
  input  S,
  input  W,
  output out_5
);

  wire and_1_out, and_2_out, and_3_out, and_4_out, not_1_out, not_2_out, not_3_out, not_4_out;

  not not_1 (not_1_out, N);
  not not_2 (not_2_out, E);
  not not_3 (not_3_out, S);
  and and_1 (and_1_out, not_1_out, E, S, W);
  not not_4 (not_4_out, W);
  and and_2 (and_2_out, N, not_2_out, S, W);
  and and_3 (and_3_out, N, E, not_3_out, W);
  and and_4 (and_4_out, N, E, S, not_4_out);
  or or_1 (out_5, and_1_out, and_2_out, and_3_out, and_4_out);
endmodule

module test (
  input  N,
  input  E,
  input  S,
  input  W,
  output first_circuit,
  output second_circuit
);

  main main_1 (.N(N), .E(E), .S(S), .W(W), .out_5(first_circuit));
  other other_1 (.N(N), .E(E), .S(S), .W(W), .out_5(second_circuit));
endmodule
