// Logisim project workshop.circ as structural Verilog: 8 circuits, main circuit Bottom
module main (
  input  a,
  input  b,
  input  c,
  input  d
);

  wire bottom_1_out_5, bottom_left_1_out_5, bottom_right_1_out_5, middle_1_out_5, top_1_out_5,
       top_left_1_out_5, top_right_1_out_5;

  Top_right top_right_1 (.a(a), .b(b), .c(c), .d(d), .out_5(top_right_1_out_5));
  Top top_1 (.a(a), .b(b), .c(c), .d(d), .out_5(top_1_out_5));
  Top_left top_left_1 (.a(a), .b(b), .c(c), .d(d), .out_5(top_left_1_out_5));
  Middle middle_1 (.a(a), .b(b), .c(c), .d(d), .out_5(middle_1_out_5));
  Bottom_left bottom_left_1 (.a(a), .b(b), .c(c), .d(d), .out_5(bottom_left_1_out_5));
  Bottom bottom_1 (.a(a), .b(b), .c(c), .d(d), .out_5(bottom_1_out_5));
  Bottom_right bottom_right_1 (.a(a), .b(b), .c(c), .d(d), .out_5(bottom_right_1_out_5));
  _7_Segment_Display u_7_segment_display_1 (
    .g(middle_1_out_5), .f(top_left_1_out_5), .a(top_1_out_5), .b(top_right_1_out_5),
    .e(bottom_left_1_out_5), .d(bottom_1_out_5), .c(bottom_right_1_out_5));  // open: dp
endmodule

module Bottom (
  input  a,
  input  b,
  input  c,
  input  d,
  output out_5
);

  wire and_1_out, and_2_out, and_3_out, and_4_out, and_5_out, not_1_out, not_2_out, not_3_out, not_4_out;

  not not_1 (not_1_out, a);
  not not_2 (not_2_out, b);
  not not_3 (not_3_out, c);
  not not_4 (not_4_out, d);
  and and_1 (and_1_out, a, not_3_out);
  and and_2 (and_2_out, not_1_out, not_2_out, not_4_out);
  and and_3 (and_3_out, b, not_3_out, d);
  and and_4 (and_4_out, not_2_out, c, d);
  and and_5 (and_5_out, b, c, not_4_out);
  or or_1 (out_5, and_1_out, and_2_out, and_3_out, and_4_out, and_5_out);
endmodule

module Bottom_left (
  input  a,
  input  b,
  input  c,
  input  d,
  output out_5
);

  wire and_1_out, and_2_out, and_3_out, and_4_out, not_1_out, not_2_out;

  not not_1 (not_1_out, b);
  not not_2 (not_2_out, d);
  and and_1 (and_1_out, a, b);
  and and_2 (and_2_out, not_1_out, not_2_out);
  and and_3 (and_3_out, c, not_2_out);
  and and_4 (and_4_out, a, c);
  or or_1 (out_5, and_1_out, and_2_out, and_3_out, and_4_out);
endmodule

module Bottom_right (
  input  a,
  input  b,
  input  c,
  input  d,
  output out_5
);

  wire and_1_out, and_2_out, and_3_out, and_4_out, and_5_out, not_1_out, not_2_out, not_3_out;

  not not_1 (not_1_out, a);
  not not_2 (not_2_out, b);
  not not_3 (not_3_out, c);
  and and_1 (and_1_out, a, not_2_out);
  and and_2 (and_2_out, not_3_out, d);
  and and_3 (and_3_out, not_1_out, b);
  and and_4 (and_4_out, not_1_out, d);
  and and_5 (and_5_out, not_1_out, not_3_out);
  or or_1 (out_5, and_1_out, and_2_out, and_3_out, and_4_out, and_5_out);
endmodule

module Top_left (
  input  a,
  input  b,
  input  c,
  input  d,
  output out_5
);

  wire and_1_out, and_2_out, and_3_out, and_4_out, nor_1_out, not_1_out, not_2_out, not_3_out, not_4_out;

  not not_1 (not_1_out, b);
  not not_2 (not_2_out, d);
  not not_3 (not_3_out, a);
  not not_4 (not_4_out, c);
  and and_1 (and_1_out, a, c);
  and and_2 (and_2_out, a, not_1_out);
  and and_3 (and_3_out, b, not_2_out);
  nor nor_1 (nor_1_out, c, d);
  and and_4 (and_4_out, not_3_out, b, not_4_out);
  or or_1 (out_5, and_1_out, and_2_out, and_3_out, nor_1_out, and_4_out);
endmodule

module Top (
  input  a,
  input  b,
  input  c,
  input  d,
  output out_5
);

  wire and_1_out, and_2_out, and_3_out, and_4_out, and_5_out, and_6_out, not_1_out, not_2_out, not_3_out,
       not_4_out;

  not not_1 (not_1_out, a);
  not not_2 (not_2_out, b);
  not not_3 (not_3_out, c);
  not not_4 (not_4_out, d);
  and and_1 (and_1_out, a, not_2_out, not_3_out);
  and and_2 (and_2_out, not_1_out, b, d);
  and and_3 (and_3_out, a, not_4_out);
  and and_4 (and_4_out, not_1_out, c);
  and and_5 (and_5_out, b, c);
  and and_6 (and_6_out, not_2_out, not_4_out);
  or or_1 (out_5, and_1_out, and_2_out, and_3_out, and_4_out, and_5_out, and_6_out);
endmodule

module Top_right (
  input  a,
  input  b,
  input  c,
  input  d,
  output out_5
);

  wire and_1_out, and_2_out, and_3_out, and_4_out, and_5_out, not_1_out, not_2_out, not_3_out, not_4_out;

  not not_1 (not_1_out, a);
  not not_2 (not_2_out, b);
  not not_3 (not_3_out, c);
  not not_4 (not_4_out, d);
  and and_1 (and_1_out, not_2_out, not_4_out);
  and and_2 (and_2_out, a, not_3_out, d);
  and and_3 (and_3_out, not_1_out, not_3_out, not_4_out);
  and and_4 (and_4_out, not_1_out, c, d);
  and and_5 (and_5_out, not_1_out, not_2_out);
  or or_1 (out_5, and_1_out, and_2_out, and_3_out, and_4_out, and_5_out);
endmodule

module Middle (
  input  a,
  input  b,
  input  c,
  input  d,
  output out_5
);

  wire and_1_out, and_2_out, and_3_out, and_4_out, and_5_out, not_1_out, not_2_out, not_3_out, not_4_out;

  not not_1 (not_1_out, a);
  not not_2 (not_2_out, b);
  not not_3 (not_3_out, c);
  not not_4 (not_4_out, d);
  and and_1 (and_1_out, not_1_out, b, not_3_out);
  and and_2 (and_2_out, a, not_2_out);
  and and_3 (and_3_out, a, d);
  and and_4 (and_4_out, not_2_out, c);
  and and_5 (and_5_out, c, not_4_out);
  or or_1 (out_5, and_1_out, and_2_out, and_3_out, and_4_out, and_5_out);
endmodule
