// Logisim project workshop.circ as structural Verilog: 1 circuit, main circuit main
module main (
  input  In,
  output out_2,
  output out_3,
  output out_4
);

  wire and_1_out, and_2_out, and_3_out, and_4_out, clock_1_out, not_1_out, not_2_out, not_3_out, or_1_out;

  not not_1 (not_1_out, out_3);
  not not_2 (not_2_out, In);
  not not_3 (not_3_out, out_2);
  and and_1 (and_1_out, not_3_out, out_3, In);
  and and_2 (and_2_out, not_1_out, not_2_out);
  and and_3 (and_3_out, out_3, out_2, In);
  Clock clock_1 (.out(clock_1_out));
  and and_4 (and_4_out, out_2, and_2_out);
  D_Flip_Flop S_MSB (.clk(clock_1_out), .D(or_1_out), .Q(out_2));  // open: Qn, preset, en, reset
  or or_1 (or_1_out, and_1_out, and_4_out);
  D_Flip_Flop S_LSB (.clk(clock_1_out), .D(and_2_out), .Q(out_3));  // open: Qn, preset, en, reset
  D_Flip_Flop Out (.clk(clock_1_out), .D(and_3_out), .Q(out_4));  // open: Qn, preset, en, reset
endmodule
